// Logisim project regfile.circ as structural Verilog: 1 circuit, main circuit regfile
module regfile (
  input  [4:0] ReadReg1,
  input  [4:0] ReadReg2,
  input  [4:0] WriteReg,
  input  [31:0] RegWriteData,
  input  RegWEn,
  input  clk,
  output [31:0] ra,
  output [31:0] sp,
  output [31:0] t0,
  output [31:0] t1,
  output [31:0] t2,
  output [31:0] s0,
  output [31:0] s1,
  output [31:0] a0,
  output [31:0] RegReadData1,
  output [31:0] RegReadData2
);

  wire WEn1, WEn2, WEn3, WEn4, WEn5, WEn6, WEn7, WEn8, WEn9, WEn10, WEn11, WEn12, WEn13, WEn14, WEn15, WEn16,
       WEn17, WEn18, WEn19, WEn20, WEn21, WEn22, WEn23, WEn24, WEn25, WEn26, WEn27, WEn28, WEn29, WEn30,
       WEn31;
  wire [31:0] a1, a2, a3, a4, a5, a6, a7, gp, s2, s3, s4, s5, s6, s7, s8, s9, s10, s11, t3, t4, t5, t6, tp,
       x0, x0in, x1in, x2in, x3in, x4in, x5in, x6in, x7in, x8in, x9in, x10in, x11in, x12in, x13in, x14in,
       x15in, x16in, x17in, x18in, x19in, x20in, x21in, x22in, x23in, x24in, x25in, x26in, x27in, x28in,
       x29in, x30in, x31in;

  Demultiplexer #(.select(5)) demultiplexer_1 (
    .out1(WEn1), .out2(WEn2), .out3(WEn3), .out4(WEn4), .out5(WEn5), .out6(WEn6), .out7(WEn7), .out8(WEn8),
    .out9(WEn9), .out10(WEn10), .out11(WEn11), .out12(WEn12), .out13(WEn13), .out14(WEn14), .out15(WEn15),
    .out16(WEn16), .out17(WEn17), .out18(WEn18), .out19(WEn19), .out20(WEn20), .out21(WEn21), .out22(WEn22),
    .out23(WEn23), .out24(WEn24), .out25(WEn25), .out26(WEn26), .out27(WEn27), .out28(WEn28), .out29(WEn29),
    .out30(WEn30), .out31(WEn31), .in(RegWEn), .sel(WriteReg));  // open: out0
  Demultiplexer #(.select(5), .width(32)) demultiplexer_2 (
    .out0(x0in), .out1(x1in), .out2(x2in), .out3(x3in), .out4(x4in), .out5(x5in), .out6(x6in), .out7(x7in),
    .out8(x8in), .out9(x9in), .out10(x10in), .out11(x11in), .out12(x12in), .out13(x13in), .out14(x14in),
    .out15(x15in), .out16(x16in), .out17(x17in), .out18(x18in), .out19(x19in), .out20(x20in), .out21(x21in),
    .out22(x22in), .out23(x23in), .out24(x24in), .out25(x25in), .out26(x26in), .out27(x27in), .out28(x28in),
    .out29(x29in), .out30(x30in), .out31(x31in), .in(RegWriteData), .sel(WriteReg));
  Register #(.width(32)) register_1 (.D(x0in), .en(1'b0), .clk(clk), .Q(x0));  // open: clr
  Register #(.width(32)) register_2 (.D(x1in), .en(WEn1), .clk(clk), .Q(ra));  // open: clr
  Register #(.width(32)) register_3 (.D(x2in), .en(WEn2), .clk(clk), .Q(sp));  // open: clr
  Register #(.width(32)) register_4 (.D(x3in), .en(WEn3), .clk(clk), .Q(gp));  // open: clr
  Register #(.width(32)) register_5 (.D(x4in), .en(WEn4), .clk(clk), .Q(tp));  // open: clr
  Register #(.width(32)) register_6 (.D(x5in), .en(WEn5), .clk(clk), .Q(t0));  // open: clr
  Register #(.width(32)) register_7 (.D(x6in), .en(WEn6), .clk(clk), .Q(t1));  // open: clr
  Register #(.width(32)) register_8 (.D(x7in), .en(WEn7), .clk(clk), .Q(t2));  // open: clr
  Register #(.width(32)) register_9 (.D(x8in), .en(WEn8), .clk(clk), .Q(s0));  // open: clr
  Register #(.width(32)) register_10 (.D(x9in), .en(WEn9), .clk(clk), .Q(s1));  // open: clr
  Register #(.width(32)) register_11 (.D(x10in), .en(WEn10), .clk(clk), .Q(a0));  // open: clr
  Register #(.width(32)) register_12 (.D(x11in), .en(WEn11), .clk(clk), .Q(a1));  // open: clr
  Register #(.width(32)) register_13 (.D(x12in), .en(WEn12), .clk(clk), .Q(a2));  // open: clr
  Register #(.width(32)) register_14 (.D(x13in), .en(WEn13), .clk(clk), .Q(a3));  // open: clr
  Register #(.width(32)) register_15 (.D(x14in), .en(WEn14), .clk(clk), .Q(a4));  // open: clr
  Register #(.width(32)) register_16 (.D(x15in), .en(WEn15), .clk(clk), .Q(a5));  // open: clr
  Register #(.width(32)) register_17 (.D(x16in), .en(WEn16), .clk(clk), .Q(a6));  // open: clr
  Register #(.width(32)) register_18 (.D(x17in), .en(WEn17), .clk(clk), .Q(a7));  // open: clr
  Register #(.width(32)) register_19 (.D(x18in), .en(WEn18), .clk(clk), .Q(s2));  // open: clr
  Register #(.width(32)) register_20 (.D(x19in), .en(WEn19), .clk(clk), .Q(s3));  // open: clr
  Register #(.width(32)) register_21 (.D(x20in), .en(WEn20), .clk(clk), .Q(s4));  // open: clr
  Register #(.width(32)) register_22 (.D(x21in), .en(WEn21), .clk(clk), .Q(s5));  // open: clr
  Register #(.width(32)) register_23 (.D(x22in), .en(WEn22), .clk(clk), .Q(s6));  // open: clr
  Register #(.width(32)) register_24 (.D(x23in), .en(WEn23), .clk(clk), .Q(s7));  // open: clr
  Register #(.width(32)) register_25 (.D(x24in), .en(WEn24), .clk(clk), .Q(s8));  // open: clr
  Register #(.width(32)) register_26 (.D(x25in), .en(WEn25), .clk(clk), .Q(s9));  // open: clr
  Register #(.width(32)) register_27 (.D(x26in), .en(WEn26), .clk(clk), .Q(s10));  // open: clr
  Register #(.width(32)) register_28 (.D(x27in), .en(WEn27), .clk(clk), .Q(s11));  // open: clr
  Register #(.width(32)) register_29 (.D(x28in), .en(WEn28), .clk(clk), .Q(t3));  // open: clr
  Register #(.width(32)) register_30 (.D(x29in), .en(WEn29), .clk(clk), .Q(t4));  // open: clr
  Register #(.width(32)) register_31 (.D(x30in), .en(WEn30), .clk(clk), .Q(t5));  // open: clr
  Register #(.width(32)) register_32 (.D(x31in), .en(WEn31), .clk(clk), .Q(t6));  // open: clr
  Multiplexer #(.select(5), .width(32)) multiplexer_1 (
    .in0(x0), .in1(ra), .in2(sp), .in3(gp), .in4(tp), .in5(t0), .in6(t1), .in7(t2), .in8(s0), .in9(s1),
    .in10(a0), .in11(a1), .in12(a2), .in13(a3), .in14(a4), .in15(a5), .in16(a6), .in17(a7), .in18(s2),
    .in19(s3), .in20(s4), .in21(s5), .in22(s6), .in23(s7), .in24(s8), .in25(s9), .in26(s10), .in27(s11),
    .in28(t3), .in29(t4), .in30(t5), .in31(t6), .out(RegReadData1), .sel(ReadReg1));
  Multiplexer #(.select(5), .width(32)) multiplexer_2 (
    .in0(x0), .in1(ra), .in2(sp), .in3(gp), .in4(tp), .in5(t0), .in6(t1), .in7(t2), .in8(s0), .in9(s1),
    .in10(a0), .in11(a1), .in12(a2), .in13(a3), .in14(a4), .in15(a5), .in16(a6), .in17(a7), .in18(s2),
    .in19(s3), .in20(s4), .in21(s5), .in22(s6), .in23(s7), .in24(s8), .in25(s9), .in26(s10), .in27(s11),
    .in28(t3), .in29(t4), .in30(t5), .in31(t6), .out(RegReadData2), .sel(ReadReg2));

  // Notes on the sheet:
  //   INPUTS to your circuit
  //   DON'T CHANGE THE LOCATIONS OF THE INPUTS AND OUTPUTS!
  //   These are DEBUG/TEST outputs from your circuit.
  //   OUTPUTS from your circuit
endmodule
